// Logisim project Summator.circ as structural Verilog: 2 circuits, main circuit main
module main (
  input  [7:0] First,
  input  in_2,
  input  [7:0] Second,
  output [7:0] out_4
);

  wire summator_2_tran, summator_3_tran, summator_4_tran, summator_5_tran, summator_6_tran, summator_7_tran,
       summator_8_tran;

  // Probe on First
  // Probe on Second
  // Probe on out_4
  summator summator_1 (.A(First[7]), .B(Second[7]), .P(summator_2_tran), .Res(out_4[7]));  // open: Tran
  summator summator_2 (.A(First[6]), .B(Second[6]), .P(summator_3_tran), .Tran(summator_2_tran), .Res(out_4[6]));
  summator summator_3 (.A(First[5]), .B(Second[5]), .P(summator_4_tran), .Tran(summator_3_tran), .Res(out_4[5]));
  summator summator_4 (.A(First[4]), .B(Second[4]), .P(summator_5_tran), .Tran(summator_4_tran), .Res(out_4[4]));
  summator summator_5 (.A(First[3]), .B(Second[3]), .P(summator_6_tran), .Tran(summator_5_tran), .Res(out_4[3]));
  summator summator_6 (.A(First[2]), .B(Second[2]), .P(summator_7_tran), .Tran(summator_6_tran), .Res(out_4[2]));
  summator summator_7 (.A(First[1]), .B(Second[1]), .P(summator_8_tran), .Tran(summator_7_tran), .Res(out_4[1]));
  summator summator_8 (.A(First[0]), .B(Second[0]), .P(in_2), .Tran(summator_8_tran), .Res(out_4[0]));
endmodule

module summator (
  input  A,
  input  B,
  input  P,
  output Tran,
  output Res
);

  wire and_1_out, and_2_out, xor_1_out;

  xor xor_1 (xor_1_out, A, B);
  xor xor_2 (Res, xor_1_out, P);
  and and_1 (and_1_out, xor_1_out, P);
  and and_2 (and_2_out, B, A);
  xor xor_3 (Tran, and_1_out, and_2_out);
endmodule
